// Logisim project Jogo da Memória.circ as structural Verilog: 3 circuits, main circuit Jogo da Memória
module \Jogo_da_Memória  (
);

  wire _00, _01, _02, _03, _10, _11, _12, _13, _20, _21, _22, _23, _30, _31, _32, _33, A00, A01, A02, A03,
       A10, A11, A12, A13, A20, A21, A22, A23, A30, A31, A32, A33, Adicionar_A, Adicionar_B, and_7_out,
       and_8_out, and_9_out, and_10_out, and_11_out, and_12_out, and_13_out, and_14_out, and_15_out,
       and_16_out, and_17_out, and_18_out, and_19_out, and_20_out, and_21_out, and_22_out, and_23_out,
       and_24_out, and_25_out, and_26_out, and_27_out, and_28_out, and_29_out, and_31_out, and_32_out,
       and_33_out, and_34_out, and_35_out, and_36_out, and_37_out, and_38_out, and_39_out, and_40_out,
       and_41_out, and_42_out, and_43_out, and_44_out, and_45_out, and_46_out, and_49_out, and_50_out,
       and_51_out, and_52_out, and_53_out, and_54_out, and_55_out, and_56_out, and_57_out, and_58_out,
       and_59_out, and_60_out, and_61_out, and_62_out, and_63_out, and_64_out, Baixo, Cima, comparator_1_eq,
       comparator_2_eq, comparator_2_gt, comparator_2_lt, comparator_3_eq, comparator_4_eq, comparator_5_eq,
       Confirmar, d_ff_1_q, decoder_2_out0, decoder_2_out1, decoder_2_out2, decoder_2_out3, decoder_2_out4,
       decoder_2_out5, decoder_2_out6, decoder_2_out7, decoder_2_out8, decoder_2_out9, decoder_2_out10,
       decoder_2_out11, decoder_2_out12, decoder_2_out13, decoder_2_out14, decoder_2_out15, decoder_3_out0,
       decoder_3_out1, decoder_3_out2, decoder_3_out3, decoder_3_out4, decoder_3_out5, decoder_3_out6,
       decoder_3_out7, decoder_3_out8, decoder_3_out9, decoder_3_out10, decoder_3_out11, decoder_3_out12,
       decoder_3_out13, decoder_3_out14, decoder_3_out15, Direita, E1, E2, Empate, Esquerda, Estado_0,
       Estado_1, Estado_2, Jogador, Jogador_A_Venceu, Jogador_B_Venceu, \MESMA_POSIÇÃO , or_1_out, or_2_out,
       or_3_out, or_4_out, or_5_out, or_6_out, or_7_out, or_8_out, or_9_out, or_12_out, or_13_out, or_14_out,
       or_15_out, or_16_out, or_17_out, or_18_out, or_19_out, or_20_out, or_21_out, or_22_out, or_23_out,
       or_24_out, or_25_out, or_26_out, or_27_out, or_28_out, Passar_Estado, Reset, VALIDADOR;
  wire [1:0] N1X, N1Y, N2X, N2Y, X, Y;
  wire [3:0] adder_1_out, grid_to_value_1_out_3, grid_to_value_2_out_3, N00, N01, N02, N03, N10, N11, N12,
       N13, N20, N21, N22, N23, N30, N31, N32, N33, Pontos_A, Pontos_B, \Primeiro_Número ,
       secret_holder_1_out_1, secret_holder_1_out_2, secret_holder_1_out_3, secret_holder_1_out_4,
       secret_holder_1_out_5, secret_holder_1_out_6, secret_holder_1_out_7, secret_holder_1_out_8,
       secret_holder_1_out_9, secret_holder_1_out_10, secret_holder_1_out_11, secret_holder_1_out_12,
       secret_holder_1_out_13, secret_holder_1_out_14, secret_holder_1_out_15, secret_holder_1_out_16,
       \Segundo_Número ;

  or or_1 (or_1_out, Baixo, Cima);
  Counter #(.width(2), .max('h2), .trigger("falling")) counter_1 (
    .Q({E2, E1}), .clk(Passar_Estado), .clr(Reset));  // open: load, D, count, carry
  Counter #(.width(4), .max('h8)) counter_2 (
    .Q(Pontos_A), .clk(Adicionar_A), .clr(Reset));  // open: load, D, count, carry
  Counter #(.width(2), .max('h3)) counter_3 (.load(Cima), .Q(X), .clk(or_1_out), .clr(Reset));  // open: D, count, carry
  Counter #(.width(1), .max('h1), .trigger("falling")) counter_4 (
    .Q(Jogador), .clk(Estado_2), .clr(Reset));  // open: load, D, count, carry
  Counter #(.width(4), .max('h8)) counter_5 (
    .Q(Pontos_B), .clk(Adicionar_B), .clr(Reset));  // open: load, D, count, carry
  Counter #(.width(2), .max('h3)) counter_6 (
    .load(Esquerda), .Q(Y), .clk(or_2_out), .clr(Reset));  // open: D, count, carry
  or or_2 (or_2_out, Esquerda, Direita);
  Adder #(.width(4)) adder_1 (.a(Pontos_A), .b(Pontos_B), .out(adder_1_out));  // open: cin, cout
  Comparator #(.width(4), .mode("unsigned")) comparator_1 (
    .a(adder_1_out), .b(4'b1000), .eq(comparator_1_eq));  // open: gt, lt
  Comparator #(.width(4)) comparator_2 (
    .a(Pontos_A), .b(Pontos_B), .gt(comparator_2_gt), .eq(comparator_2_eq), .lt(comparator_2_lt));
  LED #(.active("false")) led_1 (.in(Jogador));
  Hex_Digit_Display hex_digit_display_1 (.value(Pontos_A));  // open: dp
  and and_1 (Jogador_A_Venceu, comparator_1_eq, comparator_2_gt);
  and and_2 (Empate, comparator_1_eq, comparator_2_eq);
  and and_3 (Jogador_B_Venceu, comparator_1_eq, comparator_2_lt);
  Button button_1 (.out(Confirmar));
  LED led_2 (.in(_00));
  Hex_Digit_Display hex_digit_display_2 (.value(N00));  // open: dp
  LED led_3 (.in(_10));
  Hex_Digit_Display hex_digit_display_3 (.value(N10));  // open: dp
  LED led_4 (.in(_20));
  Hex_Digit_Display hex_digit_display_4 (.value(N20));  // open: dp
  LED led_5 (.in(_30));
  Hex_Digit_Display hex_digit_display_5 (.value(N30));  // open: dp
  and and_4 (Estado_0, ~E1, ~E2);  // AND_Gate
  and and_5 (Estado_1, E1, ~E2);  // AND_Gate
  and and_6 (Estado_2, ~E1, E2);  // AND_Gate
  Button button_2 (.out(Cima));
  Button button_3 (.out(Esquerda));
  Button button_4 (.out(Baixo));
  LED led_6 (.in(_01));
  Hex_Digit_Display hex_digit_display_6 (.value(N01));  // open: dp
  LED led_7 (.in(_11));
  Hex_Digit_Display hex_digit_display_7 (.value(N11));  // open: dp
  LED led_8 (.in(_21));
  Hex_Digit_Display hex_digit_display_8 (.value(N21));  // open: dp
  LED led_9 (.in(_31));
  Hex_Digit_Display hex_digit_display_9 (.value(N31));  // open: dp
  Button button_5 (.out(Direita));
  LED led_10 (.in(_02));
  Hex_Digit_Display hex_digit_display_10 (.value(N02));  // open: dp
  LED led_11 (.in(_12));
  Hex_Digit_Display hex_digit_display_11 (.value(N12));  // open: dp
  LED led_12 (.in(_22));
  Hex_Digit_Display hex_digit_display_12 (.value(N22));  // open: dp
  LED led_13 (.in(_32));
  Hex_Digit_Display hex_digit_display_13 (.value(N32));  // open: dp
  Button button_6 (.out(Reset));
  LED led_14 (.in(_03));
  Hex_Digit_Display hex_digit_display_14 (.value(N03));  // open: dp
  LED led_15 (.in(_13));
  Hex_Digit_Display hex_digit_display_15 (.value(N13));  // open: dp
  LED led_16 (.in(_23));
  Hex_Digit_Display hex_digit_display_16 (.value(N23));  // open: dp
  LED led_17 (.in(_33));
  Hex_Digit_Display hex_digit_display_17 (.value(N33));  // open: dp
  LED led_18 (.in(Jogador));
  Hex_Digit_Display hex_digit_display_18 (.value(Pontos_B));  // open: dp
  LED led_19 (.in(Jogador_A_Venceu));
  LED led_20 (.in(Empate));
  LED led_21 (.in(Jogador_B_Venceu));
  and and_7 (and_7_out, ~E1, Confirmar, ~E2);  // AND_Gate
  and and_8 (and_8_out, E1, Confirmar, ~E2);  // AND_Gate
  and and_9 (and_9_out, ~E1, Confirmar, E2);  // AND_Gate
  and and_10 (and_10_out, A00, _00);
  and and_11 (and_11_out, A01, _01);
  and and_12 (and_12_out, A02, _02);
  and and_13 (and_13_out, A03, _03);
  and and_14 (and_14_out, A10, _10);
  and and_15 (and_15_out, A11, _11);
  and and_16 (and_16_out, A12, _12);
  and and_17 (and_17_out, A13, _13);
  and and_18 (and_18_out, A20, _20);
  and and_19 (and_19_out, A21, _21);
  and and_20 (and_20_out, A22, _22);
  and and_21 (and_21_out, A23, _23);
  and and_22 (and_22_out, A30, _30);
  and and_23 (and_23_out, A31, _31);
  and and_24 (and_24_out, A32, _32);
  and and_25 (and_25_out, A33, _33);
  Register #(.width(2)) register_1 (.D(X), .Q(N1X), .clk(and_26_out), .clr(or_3_out));  // open: en
  or or_3 (or_3_out, Reset, d_ff_1_q);
  and and_26 (and_26_out, and_7_out, ~VALIDADOR);  // AND_Gate
  Register #(.width(2)) register_2 (.D(X), .Q(N2X), .clk(and_27_out), .clr(or_4_out));  // open: en
  or or_4 (or_4_out, Reset, d_ff_1_q);
  and and_27 (and_27_out, and_8_out, ~VALIDADOR);  // AND_Gate
  D_Flip_Flop #(.trigger("falling")) d_ff_1 (
    .clk(and_9_out), .D(1'b1), .Q(d_ff_1_q), .reset(d_ff_1_q));  // open: Qn, preset, en
  Decoder #(.select(4)) decoder_1 (
    .out0(_00), .out1(_01), .out2(_02), .out3(_03), .out4(_10), .out5(_11), .out6(_12), .out7(_13),
    .out8(_20), .out9(_21), .out10(_22), .out11(_23), .out12(_30), .out13(_31), .out14(_32), .out15(_33),
    .sel({X, Y}));  // open: en
  Register #(.width(2)) register_3 (.D(Y), .Q(N1Y), .clk(and_26_out), .clr(or_5_out));  // open: en
  or or_5 (or_5_out, Reset, d_ff_1_q);
  Register #(.width(2)) register_4 (.D(Y), .Q(N2Y), .clk(and_27_out), .clr(or_6_out));  // open: en
  or or_6 (or_6_out, Reset, d_ff_1_q);
  or or_7 (or_7_out, and_10_out, and_11_out, and_12_out, and_13_out, and_14_out, and_15_out, and_16_out, and_17_out, and_18_out, and_19_out, and_20_out, and_21_out, and_22_out, and_23_out, and_24_out, and_25_out);
  Grid_To_Value grid_to_value_1 (.Y(N1Y), .X(N1X), .out_3(grid_to_value_1_out_3));
  Grid_To_Value grid_to_value_2 (.Y(N2Y), .X(N2X), .out_3(grid_to_value_2_out_3));
  Register #(.width(4), .trigger("falling")) register_5 (
    .D(grid_to_value_1_out_3), .Q(\Primeiro_Número ), .clk(and_26_out), .clr(or_8_out));  // open: en
  or or_8 (or_8_out, Reset, d_ff_1_q);
  Register #(.width(4), .trigger("falling")) register_6 (
    .D(grid_to_value_2_out_3), .Q(\Segundo_Número ), .clk(and_27_out), .clr(or_9_out));  // open: en
  or or_9 (or_9_out, Reset, d_ff_1_q);
  or or_10 (VALIDADOR, \MESMA_POSIÇÃO , or_7_out);
  or or_11 (Passar_Estado, and_26_out, and_27_out, d_ff_1_q);
  Secret_Holder secret_holder_1 (
    .out_1(secret_holder_1_out_1), .out_2(secret_holder_1_out_2), .out_3(secret_holder_1_out_3),
    .out_4(secret_holder_1_out_4), .out_5(secret_holder_1_out_5), .out_6(secret_holder_1_out_6),
    .out_7(secret_holder_1_out_7), .out_8(secret_holder_1_out_8), .out_9(secret_holder_1_out_9),
    .out_10(secret_holder_1_out_10), .out_11(secret_holder_1_out_11), .out_12(secret_holder_1_out_12),
    .out_13(secret_holder_1_out_13), .out_14(secret_holder_1_out_14), .out_15(secret_holder_1_out_15),
    .out_16(secret_holder_1_out_16));
  Decoder #(.select(4)) decoder_2 (
    .out0(decoder_2_out0), .out1(decoder_2_out1), .out2(decoder_2_out2), .out3(decoder_2_out3),
    .out4(decoder_2_out4), .out5(decoder_2_out5), .out6(decoder_2_out6), .out7(decoder_2_out7),
    .out8(decoder_2_out8), .out9(decoder_2_out9), .out10(decoder_2_out10), .out11(decoder_2_out11),
    .out12(decoder_2_out12), .out13(decoder_2_out13), .out14(decoder_2_out14), .out15(decoder_2_out15),
    .sel({N1X, N1Y}), .en(or_12_out));
  or or_12 (or_12_out, Estado_1, Estado_2);
  Decoder #(.select(4)) decoder_3 (
    .out0(decoder_3_out0), .out1(decoder_3_out1), .out2(decoder_3_out2), .out3(decoder_3_out3),
    .out4(decoder_3_out4), .out5(decoder_3_out5), .out6(decoder_3_out6), .out7(decoder_3_out7),
    .out8(decoder_3_out8), .out9(decoder_3_out9), .out10(decoder_3_out10), .out11(decoder_3_out11),
    .out12(decoder_3_out12), .out13(decoder_3_out13), .out14(decoder_3_out14), .out15(decoder_3_out15),
    .sel({N2X, N2Y}), .en(Estado_2));
  Comparator #(.width(2), .mode("unsigned")) comparator_3 (.a(N1Y), .b(Y), .eq(comparator_3_eq));  // open: gt, lt
  Comparator #(.width(2), .mode("unsigned")) comparator_4 (.a(N1X), .b(X), .eq(comparator_4_eq));  // open: gt, lt
  Comparator #(.width(4), .mode("unsigned")) comparator_5 (
    .a(\Primeiro_Número ), .b(\Segundo_Número ), .eq(comparator_5_eq));  // open: gt, lt
  or or_13 (or_13_out, decoder_2_out0, decoder_3_out0, A00);
  or or_14 (or_14_out, decoder_2_out1, decoder_3_out1, A01);
  or or_15 (or_15_out, decoder_2_out2, decoder_3_out2, A02);
  or or_16 (or_16_out, decoder_2_out3, decoder_3_out3, A03);
  or or_17 (or_17_out, decoder_2_out4, decoder_3_out4, A10);
  or or_18 (or_18_out, decoder_2_out5, decoder_3_out5, A11);
  or or_19 (or_19_out, decoder_2_out6, decoder_3_out6, A12);
  or or_20 (or_20_out, decoder_2_out7, decoder_3_out7, A13);
  or or_21 (or_21_out, decoder_2_out8, decoder_3_out8, A20);
  or or_22 (or_22_out, decoder_2_out9, decoder_3_out9, A21);
  or or_23 (or_23_out, decoder_2_out10, decoder_3_out10, A22);
  or or_24 (or_24_out, decoder_2_out11, decoder_3_out11, A23);
  or or_25 (or_25_out, decoder_2_out12, decoder_3_out12, A30);
  or or_26 (or_26_out, decoder_2_out13, decoder_3_out13, A31);
  or or_27 (or_27_out, decoder_2_out14, decoder_3_out14, A32);
  or or_28 (or_28_out, decoder_2_out15, decoder_3_out15, A33);
  Multiplexer #(.width(4)) multiplexer_1 (.in1(secret_holder_1_out_1), .out(N00), .sel(or_13_out));  // open: in0, en
  Multiplexer #(.width(4)) multiplexer_2 (.in1(secret_holder_1_out_2), .out(N01), .sel(or_14_out));  // open: in0, en
  Multiplexer #(.width(4)) multiplexer_3 (.in1(secret_holder_1_out_3), .out(N02), .sel(or_15_out));  // open: in0, en
  Multiplexer #(.width(4)) multiplexer_4 (.in1(secret_holder_1_out_4), .out(N03), .sel(or_16_out));  // open: in0, en
  Multiplexer #(.width(4)) multiplexer_5 (.in1(secret_holder_1_out_5), .out(N10), .sel(or_17_out));  // open: in0, en
  Multiplexer #(.width(4)) multiplexer_6 (.in1(secret_holder_1_out_6), .out(N11), .sel(or_18_out));  // open: in0, en
  Multiplexer #(.width(4)) multiplexer_7 (.in1(secret_holder_1_out_7), .out(N12), .sel(or_19_out));  // open: in0, en
  Multiplexer #(.width(4)) multiplexer_8 (.in1(secret_holder_1_out_8), .out(N13), .sel(or_20_out));  // open: in0, en
  Multiplexer #(.width(4)) multiplexer_9 (.in1(secret_holder_1_out_9), .out(N20), .sel(or_21_out));  // open: in0, en
  Multiplexer #(.width(4)) multiplexer_10 (.in1(secret_holder_1_out_10), .out(N21), .sel(or_22_out));  // open: in0, en
  Multiplexer #(.width(4)) multiplexer_11 (.in1(secret_holder_1_out_11), .out(N22), .sel(or_23_out));  // open: in0, en
  Multiplexer #(.width(4)) multiplexer_12 (.in1(secret_holder_1_out_12), .out(N23), .sel(or_24_out));  // open: in0, en
  Multiplexer #(.width(4)) multiplexer_13 (.in1(secret_holder_1_out_13), .out(N30), .sel(or_25_out));  // open: in0, en
  Multiplexer #(.width(4)) multiplexer_14 (.in1(secret_holder_1_out_14), .out(N31), .sel(or_26_out));  // open: in0, en
  Multiplexer #(.width(4)) multiplexer_15 (.in1(secret_holder_1_out_15), .out(N32), .sel(or_27_out));  // open: in0, en
  Multiplexer #(.width(4)) multiplexer_16 (.in1(secret_holder_1_out_16), .out(N33), .sel(or_28_out));  // open: in0, en
  and and_28 (and_28_out, comparator_3_eq, comparator_4_eq);
  and and_29 (and_29_out, comparator_5_eq, Estado_2);
  and and_30 (\MESMA_POSIÇÃO , ~Estado_0, and_28_out);  // AND_Gate
  and and_31 (and_31_out, and_29_out, or_13_out);
  and and_32 (and_32_out, and_29_out, or_14_out);
  and and_33 (and_33_out, and_29_out, or_15_out);
  and and_34 (and_34_out, and_29_out, or_16_out);
  and and_35 (and_35_out, and_29_out, or_17_out);
  and and_36 (and_36_out, and_29_out, or_18_out);
  and and_37 (and_37_out, and_29_out, or_19_out);
  and and_38 (and_38_out, and_29_out, or_20_out);
  and and_39 (and_39_out, and_29_out, or_21_out);
  and and_40 (and_40_out, and_29_out, or_22_out);
  and and_41 (and_41_out, and_29_out, or_23_out);
  and and_42 (and_42_out, and_29_out, or_24_out);
  and and_43 (and_43_out, and_29_out, or_25_out);
  and and_44 (and_44_out, and_29_out, or_26_out);
  and and_45 (and_45_out, and_29_out, or_27_out);
  and and_46 (and_46_out, and_29_out, or_28_out);
  and and_47 (Adicionar_B, Jogador, and_29_out);
  and and_48 (Adicionar_A, ~Jogador, and_29_out);  // AND_Gate
  Counter #(.width(1), .max('h1)) counter_7 (.Q(A00), .clk(and_49_out), .clr(Reset));  // open: load, D, count, carry
  and and_49 (and_49_out, and_31_out, ~A00);  // AND_Gate
  Counter #(.width(1), .max('h1)) counter_8 (.Q(A01), .clk(and_50_out), .clr(Reset));  // open: load, D, count, carry
  and and_50 (and_50_out, and_32_out, ~A01);  // AND_Gate
  Counter #(.width(1), .max('h1)) counter_9 (.Q(A02), .clk(and_51_out), .clr(Reset));  // open: load, D, count, carry
  and and_51 (and_51_out, and_33_out, ~A02);  // AND_Gate
  Counter #(.width(1), .max('h1)) counter_10 (.Q(A03), .clk(and_52_out), .clr(Reset));  // open: load, D, count, carry
  and and_52 (and_52_out, and_34_out, ~A03);  // AND_Gate
  Counter #(.width(1), .max('h1)) counter_11 (.Q(A10), .clk(and_53_out), .clr(Reset));  // open: load, D, count, carry
  and and_53 (and_53_out, and_35_out, ~A10);  // AND_Gate
  Counter #(.width(1), .max('h1)) counter_12 (.Q(A11), .clk(and_54_out), .clr(Reset));  // open: load, D, count, carry
  and and_54 (and_54_out, and_36_out, ~A11);  // AND_Gate
  Counter #(.width(1), .max('h1)) counter_13 (.Q(A12), .clk(and_55_out), .clr(Reset));  // open: load, D, count, carry
  and and_55 (and_55_out, and_37_out, ~A12);  // AND_Gate
  Counter #(.width(1), .max('h1)) counter_14 (.Q(A13), .clk(and_56_out), .clr(Reset));  // open: load, D, count, carry
  and and_56 (and_56_out, and_38_out, ~A13);  // AND_Gate
  Counter #(.width(1), .max('h1)) counter_15 (.Q(A20), .clk(and_57_out), .clr(Reset));  // open: load, D, count, carry
  and and_57 (and_57_out, and_39_out, ~A20);  // AND_Gate
  Counter #(.width(1), .max('h1)) counter_16 (.Q(A21), .clk(and_58_out), .clr(Reset));  // open: load, D, count, carry
  and and_58 (and_58_out, and_40_out, ~A21);  // AND_Gate
  Counter #(.width(1), .max('h1)) counter_17 (.Q(A22), .clk(and_59_out), .clr(Reset));  // open: load, D, count, carry
  and and_59 (and_59_out, and_41_out, ~A22);  // AND_Gate
  Counter #(.width(1), .max('h1)) counter_18 (.Q(A23), .clk(and_60_out), .clr(Reset));  // open: load, D, count, carry
  and and_60 (and_60_out, and_42_out, ~A23);  // AND_Gate
  Counter #(.width(1), .max('h1)) counter_19 (.Q(A30), .clk(and_61_out), .clr(Reset));  // open: load, D, count, carry
  and and_61 (and_61_out, and_43_out, ~A30);  // AND_Gate
  Counter #(.width(1), .max('h1)) counter_20 (.Q(A31), .clk(and_62_out), .clr(Reset));  // open: load, D, count, carry
  and and_62 (and_62_out, and_44_out, ~A31);  // AND_Gate
  Counter #(.width(1), .max('h1)) counter_21 (.Q(A32), .clk(and_63_out), .clr(Reset));  // open: load, D, count, carry
  and and_63 (and_63_out, and_45_out, ~A32);  // AND_Gate
  Counter #(.width(1), .max('h1)) counter_22 (.Q(A33), .clk(and_64_out), .clr(Reset));  // open: load, D, count, carry
  and and_64 (and_64_out, and_46_out, ~A33);  // AND_Gate

  // Other names for the same wires on the sheet: Estado[1:0] = {E2, E1}; Trocar_Jogador = Estado_2

  // Notes on the sheet:
  //   Variáveis
  //   A
  //   B
  //   João Gabriel de Alencar Fonseca
  //   Fabricio Elizio Lima dos Santos
  //   Circuito Seletor em Grade
  //   Game Loop
endmodule

// GV
module Grid_To_Value (
  input  [1:0] Y,
  input  [1:0] X,
  output [3:0] out_3
);

  wire [3:0] secret_holder_1_out_1, secret_holder_1_out_2, secret_holder_1_out_3, secret_holder_1_out_4,
       secret_holder_1_out_5, secret_holder_1_out_6, secret_holder_1_out_7, secret_holder_1_out_8,
       secret_holder_1_out_9, secret_holder_1_out_10, secret_holder_1_out_11, secret_holder_1_out_12,
       secret_holder_1_out_13, secret_holder_1_out_14, secret_holder_1_out_15, secret_holder_1_out_16;

  Secret_Holder secret_holder_1 (
    .out_1(secret_holder_1_out_1), .out_2(secret_holder_1_out_2), .out_3(secret_holder_1_out_3),
    .out_4(secret_holder_1_out_4), .out_5(secret_holder_1_out_5), .out_6(secret_holder_1_out_6),
    .out_7(secret_holder_1_out_7), .out_8(secret_holder_1_out_8), .out_9(secret_holder_1_out_9),
    .out_10(secret_holder_1_out_10), .out_11(secret_holder_1_out_11), .out_12(secret_holder_1_out_12),
    .out_13(secret_holder_1_out_13), .out_14(secret_holder_1_out_14), .out_15(secret_holder_1_out_15),
    .out_16(secret_holder_1_out_16));
  Multiplexer #(.select(4), .width(4)) multiplexer_1 (
    .in0(secret_holder_1_out_1), .in1(secret_holder_1_out_2), .in2(secret_holder_1_out_3),
    .in3(secret_holder_1_out_4), .in4(secret_holder_1_out_5), .in5(secret_holder_1_out_6),
    .in6(secret_holder_1_out_7), .in7(secret_holder_1_out_8), .in8(secret_holder_1_out_9),
    .in9(secret_holder_1_out_10), .in10(secret_holder_1_out_11), .in11(secret_holder_1_out_12),
    .in12(secret_holder_1_out_13), .in13(secret_holder_1_out_14), .in14(secret_holder_1_out_15),
    .in15(secret_holder_1_out_16), .out(out_3), .sel({X, Y}));  // open: en
endmodule

// SECRET
module Secret_Holder (
  output [3:0] out_1,
  output [3:0] out_2,
  output [3:0] out_3,
  output [3:0] out_4,
  output [3:0] out_5,
  output [3:0] out_6,
  output [3:0] out_7,
  output [3:0] out_8,
  output [3:0] out_9,
  output [3:0] out_10,
  output [3:0] out_11,
  output [3:0] out_12,
  output [3:0] out_13,
  output [3:0] out_14,
  output [3:0] out_15,
  output [3:0] out_16
);


  assign out_1 = 4'b1000;
  assign out_2 = 4'b0001;
  assign out_3 = 4'b0010;
  assign out_4 = 4'b0101;
  assign out_5 = 4'b0100;
  assign out_6 = 4'b0101;
  assign out_7 = 4'b0110;
  assign out_8 = 4'b0111;
  assign out_9 = 4'b0010;
  assign out_10 = 4'b0011;
  assign out_11 = 4'b0111;
  assign out_12 = 4'b0011;
  assign out_13 = 4'b0001;
  assign out_14 = 4'b1000;
  assign out_15 = 4'b0100;
  assign out_16 = 4'b0110;
endmodule
